// Logisim project Assignment2_1.circ as structural Verilog
module main (
  input  in_1,
  input  in_2,
  input  in_3,
  input  in_4,
  output out_5,
  output out_6
);

  Assignment2_1 assignment2_1_1 (.a(in_1), .b(in_2), .c(in_3), .d(in_4), .and_out(out_5), .or_out(out_6));
endmodule

// VHDL entity Assignment2_1, as the project stores it:
library ieee;
use ieee.std_logic_1164.all;
use ieee.std_logic_arith.all;
use ieee.std_logic_unsigned.all;

--entity
entity Assignment2_1 is
    port (
        a, b, c, d : in std_logic;
        and_out, or_out : out std_logic
    );
end entity Assignment2_1;

--architecture
architecture bhv of Assignment2_1 is
begin
    and_out <= a and b and c and d;
    or_out  <= a or b or c or d;
end architecture bhv;
