// Logisim project Assignment2_2.circ as structural Verilog
module main (
  input  in_1,
  input  in_2,
  input  in_3,
  input  in_4,
  input  in_5,
  input  in_6,
  input  in_7,
  input  in_8,
  input  [2:0] in_9,
  output out_10
);

  Assignment2_2 assignment2_2_1 (
    .a(in_1), .b(in_2), .c(in_3), .d(in_4), .e(in_5), .f(in_6), .g(in_7), .h(in_8), .ch(in_9), .data(out_10));
endmodule

// VHDL entity Assignment2_2, as the project stores it:
library ieee;
use ieee.std_logic_1164.all;

entity Assignment2_2 is
    port (
        a, b, c, d, e, f, g, h : in std_logic;
        ch : in std_logic_vector(2 downto 0);
        data : out std_logic
    );
end entity Assignment2_2;

architecture bhv of Assignment2_2 is
begin
    process(a,b,c,d,e,f,g,h,ch)
    begin
        case ch is
            when "000" => data <= a;
            when "001" => data <= b;
            when "010" => data <= c;
            when "011" => data <= d;
            when "100" => data <= e;
            when "101" => data <= f;
            when "110" => data <= g;
            when "111" => data <= h;
            when others => data <= '0';
        end case;
    end process;
end architecture bhv;
