// Logisim project Assignment2_3.circ as structural Verilog
module main (
  input  in_1,
  input  [2:0] in_2,
  output [7:0] out_3
);

  Assignment2_3 assignment2_3_1 (.en(in_1), .dat(in_2), .display(out_3));
  _7_Segment_Display u_7_segment_display_1 (
    .g(out_3[1]), .f(out_3[2]), .a(out_3[7]), .b(out_3[6]), .e(out_3[3]), .d(out_3[4]), .c(out_3[5]),
    .dp(out_3[0]));
endmodule

// VHDL entity Assignment2_3, as the project stores it:
library ieee;
use ieee.std_logic_1164.all;

entity Assignment2_3 is
    port (
        en : in std_logic;
        dat : in std_logic_vector(2 downto 0);
        display : out std_logic_vector(7 downto 0)
    );
end entity Assignment2_3;

architecture bhv of Assignment2_3 is
begin
    process(en, dat)
    begin
        if en = '0' then
            display <= "00000000";
        else
            case dat is
                when "000" => display <= "11101110"; -- A
                when "001" => display <= "00111110"; -- b
                when "010" => display <= "10011100"; -- C
                when "011" => display <= "01111010"; -- d
                when "100" => display <= "10001110"; -- F
                when "101" => display <= "10111110"; -- G
                when others => display <= "00000000";
            end case;
        end if;
    end process;
end architecture bhv;
