// Logisim project Assignment2_5.circ as structural Verilog
module main (
  input  [12:0] in_1,
  input  en,
  output [3:0] out_3
);

  wire [7:0] assignment2_5_1_display;

  Assignment2_5 assignment2_5_1 (.vt(in_1), .en(en), .count_out(out_3), .display(assignment2_5_1_display));
  _7_Segment_Display u_7_segment_display_1 (
    .g(assignment2_5_1_display[1]), .f(assignment2_5_1_display[2]), .a(assignment2_5_1_display[7]),
    .b(assignment2_5_1_display[6]), .e(assignment2_5_1_display[3]), .d(assignment2_5_1_display[4]),
    .c(assignment2_5_1_display[5]), .dp(assignment2_5_1_display[0]));
endmodule

// VHDL entity Assignment2_5, as the project stores it:
library ieee;
use ieee.std_logic_1164.all;
use ieee.numeric_std.all;

entity Assignment2_5 is
    port (
        vt        : in  std_logic_vector(12 downto 0);
        en        : in  std_logic;
        count_out : out std_logic_vector(3 downto 0);
        display   : out std_logic_vector(7 downto 0)
    );
end entity Assignment2_5;

architecture bhv of Assignment2_5 is
begin
    process(vt, en)
        variable count : integer range 0 to 15;
    begin
        count := 0;

        for i in vt'range loop
            if vt(i) = '1' then
                count := count + 1;
            end if;
        end loop;

        count_out <= std_logic_vector(
            to_unsigned(count, 4)
        );


        if en = '0' then
            display <= "00000000";
        else
            case count is
                when 0  => display <= "11111100"; -- 0
                when 1  => display <= "01100000"; -- 1
                when 2  => display <= "11011010"; -- 2
                when 3  => display <= "11110010"; -- 3
                when 4  => display <= "01100110"; -- 4
                when 5  => display <= "10110110"; -- 5
                when 6  => display <= "10111110"; -- 6
                when 7  => display <= "11100000"; -- 7
                when 8  => display <= "11111110"; -- 8
                when 9  => display <= "11110110"; -- 9

                when 10 => display <= "11101110"; -- A
                when 11 => display <= "00111110"; -- b
                when 12 => display <= "10011100"; -- C
                when 13 => display <= "01111010"; -- d
                when 14 => display <= "10011110"; -- E
                when 15 => display <= "10001110"; -- F

                when others =>
                    display <= "00000000";
            end case;
        end if;
    end process;
end architecture bhv;
